# Fritzing sketch hw (saved by Fritzing 0.8.7b)
breadboards: 1

parts:
  PIR1 = PIR sensor
  KEYPAD1 = Membrane Matrix Keypad
  Part1 = Arduino Uno (Rev3)
  LED1 = LED - 5mm [color="Red (633nm)" package="5 mm [THT]"]
  R1 = Resistor [tolerance=±5% resistance=220 package=THT]
  PIR2 = PIR sensor
  PIR3 = PIR sensor
  LCD1 = LCD screen

nets:
  VDD: PIR1.VDD, Part1.5V, PIR2.VDD, PIR3.VDD, LCD1.VDD
  N1: PIR1.SIG, Part1.D11_PWM/MOSI
  GND: PIR1.GND, Part1.GND, LED1.cathode, PIR2.GND, PIR3.GND, LCD1.VSS
  N2: KEYPAD1.1, Part1.D8
  N3: KEYPAD1.2, Part1.D7
  N4: KEYPAD1.3, Part1.D6_PWM
  N5: KEYPAD1.4, Part1.D5_PWM
  N6: KEYPAD1.5, Part1.D4
  N7: KEYPAD1.6, Part1.D3_PWM
  N8: KEYPAD1.7, Part1.D2
  N9: Part1.A0, PIR3.SIG
  N10: Part1.D10_PWM/SS, LCD1.V0
  N11: Part1.D12/MISO, R1.Pin_1
  N12: Part1.D13/SCK, PIR2.SIG
  N13: LED1.anode, R1.Pin_0

notes:
  BUZZER
  PIR MOTION
  SENSOR
  ADKeyboard
  (5 BUTTONS)
  SERIAL LCD

custom parts:
  Membrane Matrix Keypad: Membrane Matrix 3x4 Keypad
